// Logisim project FirstAssignment_Circuit_Unit2.circ as structural Verilog: 1 circuit, main circuit main
module main (
  input  Armed,
  input  Door,
  input  Glass,
  input  Motion,
  output Alarm
);

  wire or_1_out;

  or or_1 (or_1_out, Door, Glass, Motion);
  and and_1 (Alarm, Armed, or_1_out);
endmodule
