// Logisim project Assignment2.circ as structural Verilog: 1 circuit, main circuit main
module main (
  input  A0,
  input  B0,
  input  A1,
  input  B1,
  input  A2,
  input  B2,
  input  A3,
  input  B3,
  output S0,
  output S1,
  output S2,
  output S3,
  output out_13
);

  wire and_1_out, and_2_out, and_3_out, and_4_out, and_5_out, and_6_out, and_7_out, and_8_out, and_9_out,
       and_10_out, and_11_out, and_12_out, not_1_out, not_2_out, not_3_out, not_4_out, or_1_out, or_2_out,
       or_3_out, or_4_out, xor_1_out, xor_2_out, xor_3_out, xor_4_out, xor_5_out, xor_6_out, xor_7_out,
       xor_9_out, xor_10_out, xor_11_out;

  not not_1 (not_1_out, B0);
  not not_2 (not_2_out, B1);
  not not_3 (not_3_out, B2);
  not not_4 (not_4_out, B3);
  and and_1 (and_1_out, 1'b1, not_1_out);
  and and_2 (and_2_out, 1'b0, not_2_out);
  and and_3 (and_3_out, 1'b0, not_3_out);
  xor xor_1 (xor_1_out, 1'b1, not_1_out);
  xor xor_2 (xor_2_out, 1'b0, not_2_out);
  xor xor_3 (xor_3_out, 1'b0, not_3_out);
  xor xor_4 (xor_4_out, 1'b0, not_4_out);
  xor xor_5 (xor_5_out, xor_2_out, and_1_out);
  and and_4 (and_4_out, and_1_out, xor_2_out);
  xor xor_6 (xor_6_out, xor_3_out, or_1_out);
  and and_5 (and_5_out, or_1_out, xor_3_out);
  xor xor_7 (xor_7_out, xor_4_out, or_2_out);
  or or_1 (or_1_out, and_4_out, and_2_out);
  or or_2 (or_2_out, and_5_out, and_3_out);
  xor xor_8 (S0, A0, xor_1_out);
  and and_6 (and_6_out, A0, xor_1_out);
  xor xor_9 (xor_9_out, A1, xor_5_out);
  and and_7 (and_7_out, A1, xor_5_out);
  xor xor_10 (xor_10_out, A2, xor_6_out);
  and and_8 (and_8_out, A2, xor_6_out);
  xor xor_11 (xor_11_out, A3, xor_7_out);
  and and_9 (and_9_out, A3, xor_7_out);
  xor xor_12 (S1, xor_9_out, and_6_out);
  and and_10 (and_10_out, and_6_out, xor_9_out);
  xor xor_13 (S2, xor_10_out, or_3_out);
  and and_11 (and_11_out, or_3_out, xor_10_out);
  xor xor_14 (S3, xor_11_out, or_4_out);
  and and_12 (and_12_out, or_4_out, xor_11_out);
  or or_3 (or_3_out, and_10_out, and_7_out);
  or or_4 (or_4_out, and_11_out, and_8_out);
  or or_5 (out_13, and_12_out, and_9_out);

  // Notes on the sheet:
  //   S4 (this bit is overflowed when two inputs are the same number)
endmodule
