// Logisim project 4bitRegister.circ as structural Verilog: 1 circuit, main circuit main
module main (
  input  Control,
  input  D_Input1,
  input  D_Input2,
  input  D_Input3,
  input  D_Input4,
  output D_Output1,
  output D_Output2,
  output D_Output3,
  output D_Output4
);

  wire clock_1_out;

  Clock clock_1 (.out(clock_1_out));
  D_Flip_Flop d_ff_1 (.clk(clock_1_out), .D(D_Input1), .Q(D_Output1), .en(Control));  // open: Qn, preset, reset
  D_Flip_Flop d_ff_2 (.clk(clock_1_out), .D(D_Input2), .Q(D_Output2), .en(Control));  // open: Qn, preset, reset
  D_Flip_Flop d_ff_3 (.clk(clock_1_out), .D(D_Input3), .Q(D_Output3), .en(Control));  // open: Qn, preset, reset
  D_Flip_Flop d_ff_4 (.clk(clock_1_out), .D(D_Input4), .Q(D_Output4), .en(Control));  // open: Qn, preset, reset

  // Notes on the sheet:
  //   Clock
endmodule
